// Logisim project cod_oel.circ as structural Verilog: 7 circuits, main circuit main
module main (
  input  enable,
  output zero_flag
);

  wire alu_slt, clock_1_out, main_cu_1_alusrc, main_cu_1_memread, main_cu_1_memtoreg, main_cu_1_memwrite,
       main_cu_1_regdst, main_cu_1_regwrite;
  wire [1:0] main_cu_1_aluop0;
  wire [2:0] alucu_1_aluoperation;
  wire [4:0] multiplexer_1_out;
  wire [31:0] alu_aluresult, bit_extender_1_out, data_memory_readdata, instruction_fetch_ir,
       multiplexer_2_out, multiplexer_3_out, register_file_readdata1, register_file_readdata2;

  Clock clock_1 (.out(clock_1_out));
  instruction_fetch instruction_fetch (.clock(clock_1_out), .ENABLE(enable), .IR(instruction_fetch_ir));
  // Probe on instruction_fetch_ir
  // Probe on instruction_fetch_ir[25:21]
  // Probe on instruction_fetch_ir[20:16]
  Multiplexer #(.width(5), .enable("false")) multiplexer_1 (
    .in0(instruction_fetch_ir[20:16]), .in1(instruction_fetch_ir[15:11]), .out(multiplexer_1_out),
    .sel(main_cu_1_regdst));
  // Probe on instruction_fetch_ir[15:11]
  register_file register_file (
    .write(main_cu_1_regwrite), .clock(clock_1_out), .ReadReg1(instruction_fetch_ir[25:21]),
    .writedata(multiplexer_3_out), .ReadReg2(instruction_fetch_ir[20:16]), .WriteRegister(multiplexer_1_out),
    .ReadData1(register_file_readdata1), .ReadData2(register_file_readdata2));
  assign bit_extender_1_out = {{16{1'b0}}, instruction_fetch_ir[15:0]};  // Bit_Extender bit_extender_1
  // Probe on main_cu_1_regwrite
  // Probe on register_file_readdata1
  // Probe on register_file_readdata2
  // Probe on bit_extender_1_out
  main_cu main_cu_1 (
    .opcode(instruction_fetch_ir[31:26]), .regwrite(main_cu_1_regwrite), .regdst(main_cu_1_regdst),
    .alusrc(main_cu_1_alusrc), .memtoreg(main_cu_1_memtoreg), .memread(main_cu_1_memread),
    .memwrite(main_cu_1_memwrite), .aluop1(main_cu_1_aluop0[1]), .aluop0(main_cu_1_aluop0[0]));  // open: branch, jump
  Multiplexer #(.width(32), .enable("false")) multiplexer_2 (
    .in0(register_file_readdata2), .in1(bit_extender_1_out), .out(multiplexer_2_out), .sel(main_cu_1_alusrc));
  ALU alu (
    .aluOperation(alucu_1_aluoperation), .src1(register_file_readdata1), .slt(alu_slt),
    .src2(multiplexer_2_out), .zero_flag(zero_flag), .AluResult(alu_aluresult));
  // Probe on multiplexer_2_out
  // Probe on main_cu_1_alusrc
  alucu alucu_1 (.aluop(main_cu_1_aluop0), .funct(instruction_fetch_ir[5:0]), .aluoperation(alucu_1_aluoperation));
  // Probe on alu_aluresult
  datamemory data_memory (
    .address(alu_aluresult), .writedata(register_file_readdata2), .memread(main_cu_1_memread),
    .memwrite(main_cu_1_memwrite), .clock(clock_1_out), .readdata(data_memory_readdata));
  // Probe on alu_slt
  Multiplexer #(.width(32), .enable("false")) multiplexer_3 (
    .in0(alu_aluresult), .in1(data_memory_readdata), .out(multiplexer_3_out), .sel(main_cu_1_memtoreg));
  // Probe on multiplexer_3_out
endmodule

module register_file (
  input  write,
  input  clock,
  input  [4:0] ReadReg1,
  input  [31:0] writedata,
  input  [4:0] ReadReg2,
  input  [4:0] WriteRegister,
  output [31:0] ReadData1,
  output [31:0] ReadData2
);

  wire and_1_out, and_2_out, and_3_out, and_4_out, and_5_out, and_6_out, and_7_out, and_8_out, and_9_out,
       and_10_out, and_11_out, and_12_out, and_13_out, and_14_out, and_15_out, and_16_out, and_17_out,
       and_18_out, and_19_out, and_20_out, and_21_out, and_22_out, and_23_out, and_24_out, and_25_out,
       and_26_out, and_27_out, and_28_out, and_29_out, and_30_out, and_31_out, and_32_out, decoder_1_out0,
       decoder_1_out1, decoder_1_out2, decoder_1_out3, decoder_1_out4, decoder_1_out5, decoder_1_out6,
       decoder_1_out7, decoder_1_out8, decoder_1_out9, decoder_1_out10, decoder_1_out11, decoder_1_out12,
       decoder_1_out13, decoder_1_out14, decoder_1_out15, decoder_1_out16, decoder_1_out17, decoder_1_out18,
       decoder_1_out19, decoder_1_out20, decoder_1_out21, decoder_1_out22, decoder_1_out23, decoder_1_out24,
       decoder_1_out25, decoder_1_out26, decoder_1_out27, decoder_1_out28, decoder_1_out29, decoder_1_out30,
       decoder_1_out31;
  wire [31:0] a0_q, a1_q, a2_q, a3_q, at_q, fp_q, gp_q, k0_q, k1_q, ra_q, s0_q, s1_q, s2_q, s3_q, s4_q, s5_q,
       s6_q, s7_q, t0_q, t1_q, t2_q, t3_q, t4_q, t5_q, t6_q, t7_q, t8_q, t9_q, undriven, v0_q, v1_q, zero_q;

  Decoder #(.select(5)) decoder_1 (
    .out0(decoder_1_out0), .out1(decoder_1_out1), .out2(decoder_1_out2), .out3(decoder_1_out3),
    .out4(decoder_1_out4), .out5(decoder_1_out5), .out6(decoder_1_out6), .out7(decoder_1_out7),
    .out8(decoder_1_out8), .out9(decoder_1_out9), .out10(decoder_1_out10), .out11(decoder_1_out11),
    .out12(decoder_1_out12), .out13(decoder_1_out13), .out14(decoder_1_out14), .out15(decoder_1_out15),
    .out16(decoder_1_out16), .out17(decoder_1_out17), .out18(decoder_1_out18), .out19(decoder_1_out19),
    .out20(decoder_1_out20), .out21(decoder_1_out21), .out22(decoder_1_out22), .out23(decoder_1_out23),
    .out24(decoder_1_out24), .out25(decoder_1_out25), .out26(decoder_1_out26), .out27(decoder_1_out27),
    .out28(decoder_1_out28), .out29(decoder_1_out29), .out30(decoder_1_out30), .out31(decoder_1_out31),
    .sel(WriteRegister));  // open: en
  and and_1 (and_1_out, write, decoder_1_out0);
  and and_2 (and_2_out, write, decoder_1_out1);
  and and_3 (and_3_out, write, decoder_1_out2);
  and and_4 (and_4_out, write, decoder_1_out3);
  and and_5 (and_5_out, write, decoder_1_out4);
  and and_6 (and_6_out, write, decoder_1_out5);
  and and_7 (and_7_out, write, decoder_1_out6);
  and and_8 (and_8_out, write, decoder_1_out7);
  and and_9 (and_9_out, write, decoder_1_out8);
  and and_10 (and_10_out, write, decoder_1_out9);
  and and_11 (and_11_out, write, decoder_1_out10);
  and and_12 (and_12_out, write, decoder_1_out11);
  and and_13 (and_13_out, write, decoder_1_out12);
  and and_14 (and_14_out, write, decoder_1_out13);
  and and_15 (and_15_out, write, decoder_1_out14);
  and and_16 (and_16_out, write, decoder_1_out15);
  and and_17 (and_17_out, write, decoder_1_out16);
  and and_18 (and_18_out, write, decoder_1_out17);
  and and_19 (and_19_out, write, decoder_1_out18);
  and and_20 (and_20_out, write, decoder_1_out19);
  and and_21 (and_21_out, write, decoder_1_out20);
  and and_22 (and_22_out, write, decoder_1_out21);
  and and_23 (and_23_out, write, decoder_1_out22);
  and and_24 (and_24_out, write, decoder_1_out23);
  and and_25 (and_25_out, write, decoder_1_out24);
  and and_26 (and_26_out, write, decoder_1_out25);
  and and_27 (and_27_out, write, decoder_1_out26);
  and and_28 (and_28_out, write, decoder_1_out27);
  and and_29 (and_29_out, write, decoder_1_out28);
  and and_30 (and_30_out, write, decoder_1_out29);
  and and_31 (and_31_out, write, decoder_1_out30);
  and and_32 (and_32_out, write, decoder_1_out31);
  Register #(.width(32)) zero (.D(writedata), .en(and_1_out), .Q(zero_q), .clk(clock));  // open: clr
  Register #(.width(32)) at (.D(writedata), .en(and_2_out), .Q(at_q), .clk(clock));  // open: clr
  Register #(.width(32)) v0 (.D(writedata), .en(and_3_out), .Q(v0_q), .clk(clock));  // open: clr
  Register #(.width(32)) v1 (.D(writedata), .en(and_4_out), .Q(v1_q), .clk(clock));  // open: clr
  Register #(.width(32)) a0 (.D(writedata), .en(and_5_out), .Q(a0_q), .clk(clock));  // open: clr
  Register #(.width(32)) a1 (.D(writedata), .en(and_6_out), .Q(a1_q), .clk(clock));  // open: clr
  Register #(.width(32)) a2 (.D(writedata), .en(and_7_out), .Q(a2_q), .clk(clock));  // open: clr
  Register #(.width(32)) a3 (.D(writedata), .en(and_8_out), .Q(a3_q), .clk(clock));  // open: clr
  Register #(.width(32)) t0 (.D(writedata), .en(and_9_out), .Q(t0_q), .clk(clock));  // open: clr
  Register #(.width(32)) t1 (.D(writedata), .en(and_10_out), .Q(t1_q), .clk(clock));  // open: clr
  Register #(.width(32)) t2 (.D(writedata), .en(and_11_out), .Q(t2_q), .clk(clock));  // open: clr
  Register #(.width(32)) t3 (.D(writedata), .en(and_12_out), .Q(t3_q), .clk(clock));  // open: clr
  Register #(.width(32)) t4 (.D(writedata), .en(and_13_out), .Q(t4_q), .clk(clock));  // open: clr
  Register #(.width(32)) t5 (.D(writedata), .en(and_14_out), .Q(t5_q), .clk(clock));  // open: clr
  Register #(.width(32)) t6 (.D(writedata), .en(and_15_out), .Q(t6_q), .clk(clock));  // open: clr
  Register #(.width(32)) t7 (.D(writedata), .en(and_16_out), .Q(t7_q), .clk(clock));  // open: clr
  Register #(.width(32)) s0 (.D(writedata), .en(and_17_out), .Q(s0_q), .clk(clock));  // open: clr
  Register #(.width(32)) s1 (.D(writedata), .en(and_18_out), .Q(s1_q), .clk(clock));  // open: clr
  Register #(.width(32)) s2 (.D(writedata), .en(and_19_out), .Q(s2_q), .clk(clock));  // open: clr
  Register #(.width(32)) s3 (.D(writedata), .en(and_20_out), .Q(s3_q), .clk(clock));  // open: clr
  Register #(.width(32)) s4 (.D(writedata), .en(and_21_out), .Q(s4_q), .clk(clock));  // open: clr
  Register #(.width(32)) s5 (.D(writedata), .en(and_22_out), .Q(s5_q), .clk(clock));  // open: clr
  Register #(.width(32)) s6 (.D(writedata), .en(and_23_out), .Q(s6_q), .clk(clock));  // open: clr
  Register #(.width(32)) s7 (.D(writedata), .en(and_24_out), .Q(s7_q), .clk(clock));  // open: clr
  Register #(.width(32)) t8 (.D(writedata), .en(and_25_out), .Q(t8_q), .clk(clock));  // open: clr
  Register #(.width(32)) t9 (.D(writedata), .en(and_26_out), .Q(t9_q), .clk(clock));  // open: clr
  Register #(.width(32)) k0 (.D(writedata), .en(and_27_out), .Q(k0_q), .clk(clock));  // open: clr
  Register #(.width(32)) k1 (.D(writedata), .en(and_28_out), .Q(k1_q), .clk(clock));  // open: clr
  Register #(.width(32)) gp (.D(writedata), .en(and_29_out), .Q(gp_q), .clk(clock));  // open: clr
  Register #(.width(32)) sp (.D(writedata), .en(and_30_out), .clk(clock));  // open: Q, clr
  Register #(.width(32)) fp (.D(writedata), .en(and_31_out), .Q(fp_q), .clk(clock));  // open: clr
  Register #(.width(32)) ra (.D(writedata), .en(and_32_out), .Q(ra_q), .clk(clock));  // open: clr
  Multiplexer #(.select(5), .width(32), .enable("false")) multiplexer_1 (
    .in0(zero_q), .in1(at_q), .in2(v0_q), .in3(v1_q), .in4(a0_q), .in5(a1_q), .in6(a2_q), .in7(a3_q),
    .in8(t0_q), .in9(t1_q), .in10(t2_q), .in11(t3_q), .in12(t4_q), .in13(t5_q), .in14(t6_q), .in15(t7_q),
    .in16(s0_q), .in17(s1_q), .in18(s2_q), .in19(s3_q), .in20(s4_q), .in21(s5_q), .in22(s6_q), .in23(s7_q),
    .in24(t8_q), .in25(t9_q), .in26(k0_q), .in27(k1_q), .in28(gp_q), .in29(undriven), .in30(fp_q),
    .in31(ra_q), .out(ReadData1), .sel(ReadReg1));
  Multiplexer #(.select(5), .width(32), .enable("false")) multiplexer_2 (
    .in0(zero_q), .in1(at_q), .in2(v0_q), .in3(v1_q), .in4(a0_q), .in5(a1_q), .in6(a2_q), .in7(a3_q),
    .in8(t0_q), .in9(t1_q), .in10(t2_q), .in11(t3_q), .in12(t4_q), .in13(t5_q), .in14(t6_q), .in15(t7_q),
    .in16(s0_q), .in17(s1_q), .in18(s2_q), .in19(s3_q), .in20(s4_q), .in21(s5_q), .in22(s6_q), .in23(s7_q),
    .in24(t8_q), .in25(t9_q), .in26(k0_q), .in27(k1_q), .in28(gp_q), .in29(undriven), .in30(fp_q),
    .in31(ra_q), .out(ReadData2), .sel(ReadReg2));
endmodule

module ALU (
  input  [2:0] aluOperation,
  input  [31:0] src1,
  input  [31:0] src2,
  output zero_flag,
  output slt,
  output [31:0] AluResult
);

  wire [31:0] adder_1_out, adder_2_out, and_1_out, bit_extender_1_out, not_1_out, or_1_out;

  assign not_1_out = ~src2;  // NOT_Gate not_1, 32 bits wide
  assign and_1_out = src1 & src2;  // AND_Gate and_1, 32 bits wide
  assign or_1_out = src1 | src2;  // OR_Gate or_1, 32 bits wide
  Adder #(.width(32)) adder_1 (.a(src1), .b(src2), .out(adder_1_out));  // open: cin, cout
  Adder #(.width(32)) adder_2 (.a(src1), .b(not_1_out), .out(adder_2_out), .cin(1'b1));  // open: cout
  Multiplexer #(.select(3), .width(32), .enable("false")) multiplexer_1 (
    .in0(and_1_out), .in1(or_1_out), .in2(adder_1_out), .in6(adder_2_out), .in7(bit_extender_1_out),
    .out(AluResult), .sel(aluOperation));  // open: in3, in4, in5
  assign bit_extender_1_out = {{31{1'b0}}, adder_2_out[31]};  // Bit_Extender bit_extender_1
  Comparator #(.width(32)) comparator_1 (.a({32{1'b0}}), .b(AluResult), .eq(zero_flag), .lt(slt));  // open: gt
endmodule

module instruction_fetch (
  input  clock,
  input  ENABLE,
  output [31:0] IR
);

  wire [31:0] adder_1_out, PC_q;

  Register #(.width(32)) PC (.D(adder_1_out), .Q(PC_q), .clk(clock));  // open: en, clr
  RAM #(.addrWidth(24), .dataWidth(32)) ram_1 (
    .addr(PC_q[23:0]), .data(IR), .clk(clock), .ld(ENABLE));  // open: sel, clr
  Adder #(.width(32)) adder_1 (.a(PC_q), .b(32'h4), .out(adder_1_out));  // open: cin, cout
endmodule

module datamemory (
  input  [31:0] address,
  input  [31:0] writedata,
  input  memread,
  input  memwrite,
  input  clock,
  output [31:0] readdata
);

  RAM #(.addrWidth(24), .dataWidth(32), .bus("separate")) ram_1 (
    .addr(address[23:0]), .din(writedata), .data(readdata), .str(memwrite), .clk(clock), .ld(memread));  // open: sel, clr
endmodule

module alucu (
  input  [1:0] aluop,
  input  [5:0] funct,
  output [2:0] aluoperation
);

  wire and_1_out, not_1_out, not_2_out, or_1_out;

  and and_1 (and_1_out, aluop[1], funct[1]);
  and and_2 (aluoperation[0], aluop[1], or_1_out);
  or or_1 (or_1_out, funct[0], funct[3]);
  not not_1 (not_1_out, aluop[1]);
  not not_2 (not_2_out, funct[2]);
  or or_2 (aluoperation[2], aluop[0], and_1_out);
  or or_3 (aluoperation[1], not_1_out, not_2_out);
endmodule

module main_cu (
  input  [5:0] opcode,
  output regwrite,
  output regdst,
  output alusrc,
  output memtoreg,
  output memread,
  output memwrite,
  output branch,
  output jump,
  output aluop1,
  output aluop0
);

  wire and_1_out, and_2_out, not_1_out, not_2_out, not_3_out, not_4_out, not_5_out, not_6_out;

  not not_1 (not_1_out, opcode[5]);
  not not_2 (not_2_out, opcode[4]);
  not not_3 (not_3_out, opcode[3]);
  not not_4 (not_4_out, opcode[2]);
  not not_5 (not_5_out, opcode[1]);
  not not_6 (not_6_out, opcode[0]);
  and and_1 (and_1_out, not_4_out, not_5_out);
  and and_2 (and_2_out, opcode[5], not_4_out, not_3_out);
  and and_3 (memread, opcode[5], not_3_out);
  and and_4 (memwrite, opcode[5], opcode[3]);
  and and_5 (jump, opcode[0], not_5_out);
  and and_6 (aluop1, not_5_out, not_4_out);
  or or_1 (regwrite, and_1_out, and_2_out);

  assign aluop0 = opcode[2];
  assign alusrc = opcode[0];
  assign branch = opcode[2];
  assign memtoreg = opcode[0];
  assign regdst = aluop1;
endmodule
